# Fritzing sketch intercom (saved by Fritzing 0.7.4b)
breadboards: 1

parts:
  LM386 = IC, DIP package, 8 pins [chip_label=IC spacing=300mil]
  C4 = Electrolytic Capacitor [capacitance=0.1µF voltage=63V package="100 mil [THT, electrolytic]"]
  R2 = Resistor [tolerance=±5% resistance=10k package=THT]
  R4 = Resistor [tolerance=±5% resistance=220 package=THT]  # not connected
  R5 = Resistor [tolerance=±5% resistance=220 package=THT]  # not connected
  R6 = Resistor [tolerance=±5% resistance=220 package=THT]  # not connected
  C2 = Electrolytic Capacitor [capacitance=220µF voltage=16V package="100 mil [THT, electrolytic]"]
  C3 = Ceramic Capacitor [capacitance=47nF package="100 mil [THT, multilayer]"]
  R1 = Resistor [tolerance=±1% resistance=10 package=THT]
  R3 = Resistor [tolerance=±5% resistance=10k package=THT]
  C5 = Ceramic Capacitor [capacitance=47nF package="100 mil [THT, multilayer]"]
  C1 = Electrolytic Capacitor [capacitance=0.1µF voltage=63V package="100 mil [THT, electrolytic]"]

nets (from the pcb view):
  N1: LM386.pin1, C1.+
  N2: LM386.pin2, LM386.pin4, C4.-, C3.0
  N3: LM386.pin3, R2.Pin_0
  N4: LM386.pin5, C2.+, R1.Pin_0
  N5: LM386.pin6, R3.Pin_0
  N6: LM386.pin7, C4.+
  N7: R2.Pin_1, C5.0
  N8: C3.1, R1.Pin_1
  N9: R3.Pin_1, C5.1
